# Fritzing sketch ferronron (saved by Fritzing 0.9.3b)
breadboards: 1

parts:
  Raspberry_Pi_1 = Raspberry Pi 3 [part_number=RPI-3-V1.2]
  S1 = Taiway 100-SP-X-T1 SPDT Miniature Toggle Switch [part_number=100-SP-X-T1-0-0-B1-M1 package=THT]
  S2 = Taiway 100-SP-X-T1 SPDT Miniature Toggle Switch [part_number=100-SP-X-T1-0-0-B1-M1 package=THT]
  R2 = Resistor [tolerance=±5% resistance=330 package=THT]
  R3 = Resistor [tolerance=±5% resistance=330 package=THT]
  R4 = Resistor [tolerance=±5% resistance=10k package=THT]
  R5 = Resistor [tolerance=±5% resistance=330 package=THT]
  Power_plug1 = Power plug
  R6 = Resistor [tolerance=±5% resistance=10k package=THT]
  R7 = Resistor [tolerance=±5% resistance=10k package=THT]
  S3 = Pushbutton [package="[THT]"]

nets:
  3V3: Raspberry_Pi_1.3v3, Raspberry_Pi_1.3V3, S1.COM, R5.Pin_1
  GND: Raspberry_Pi_1.GND, R4.Pin_0, Power_plug1.GND, R6.Pin_1, R7.Pin_1
  N1: Raspberry_Pi_1.GPIO17, R2.Pin_1, R7.Pin_0
  N2: Raspberry_Pi_1.GPIO27, R3.Pin_1, R6.Pin_0
  N3: Raspberry_Pi_1.GPIO18, R4.Pin_1, S3.Pin_1, S3.Pin_2
  N4: Raspberry_Pi_1.5V, S2.L2
  N5: S1.L1, R3.Pin_0
  N6: S1.L2, R2.Pin_0
  5V: S2.COM, Power_plug1.VCC
  N7: R5.Pin_0, S3.Pin_3, S3.Pin_4
